# Fritzing sketch TRH (saved by Fritzing 0.9.3b)
breadboards: 2

parts:
  microSD_Transflash1 = SparkFun - microSD Transflash
  R1 = Temperature Sensor (Thermistor) [thermistor_type=NTC package=THT]  # not connected
  Q1 = TRANSISTOR_NPN [package=to-92]  # not connected
  LED1 = LED - 3mm [color="Red (633nm)" package="3 mm [THT]"]  # not connected
  JP1 = Header 12 [package=1x12_machine-pin-header_lock.004]  # not connected
  JP2 = Header 12 [package=1x12_machine-pin-header_lock.004]  # not connected
  JP3 = Header 12 [package=1x12_machine-pin-header_lock.004]  # not connected
  JP4 = Header 12 [package=1x12_machine-pin-header_lock.004]  # not connected
  Bauteil7 = DeadOn RTC - DS3234 Breakout
  JP5 = Header 4 [package=1x12_machine-pin-header_lock.004]  # not connected
  JP7 = Header 4 [package=1x12_machine-pin-header_lock.004]  # not connected
  Bauteil10 = Triple Axis Magnetometer - HMC5883 Breakout - MyAccelerometer  # not connected
  Bauteil11 = SHT1x-Breakout  # not connected
  Bauteil14 = SHT1x-Breakout
  Bauteil15 = Arduino Pro Mini v13

nets:
  N1: microSD_Transflash1.GND, Bauteil14.DATA
  N2: microSD_Transflash1.SCK, Bauteil7.SCLK, Bauteil15.D13/SCK
  VCC: microSD_Transflash1.VCC, Bauteil7.VCC, Bauteil14.SCK, Bauteil15.VCC
  N3: microSD_Transflash1.DI, Bauteil7.MOSI, Bauteil15.D11_PWM/MOSI
  N4: microSD_Transflash1.CS, Bauteil15.D9_PWM
  GND: Bauteil7.GND, Bauteil15.GND
  N5: Bauteil7.INT/SQW, Bauteil15.D8
  N6: Bauteil7.MISO, Bauteil15.D12/MISO
  N7: Bauteil7.SS, Bauteil15.D10_PWM/SS
  N8: Bauteil14.GND, Bauteil15.D4

custom parts:
  DeadOn RTC - DS3234 Breakout: Description: Here is a real time clock based on the DS3234 Real Time Clock IC. The DS3234 is a low-cost, extremely accurate SPI bus real-time clock with an integrated temperature-compensated crystal oscillator and crystal. The RTC maintains seconds, minutes, hours, day, date, month, and year information. The date at the end of the month is automatically adjusted for months with fewer than 31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
  Header 4: Header 12 Standard 12-pin 0.1 header. Use with straight break away headers (SKU : PRT-00116), right angle break away headers (PRT-00553), swiss pins (PRT-00743), machine pins (PRT-00117), and female headers (PRT-00115).
  Triple Axis Magnetometer - HMC5883 Breakout - MyAccelerometer: This is a breakout board for Honeywell's HMC5883, a 3-axis digital compass. Communication with the HMC5883 is simple and all done through an I2C interface. There is no on-board regulator, so a regulated voltage of 2.16-3.6VDC should be supplied. The breakout board includes the HMC584843 sensor and all filtering capacitors as shown. The power and 2-wire interface pins are all broken out to a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
  SHT1x-Breakout: The SHT15 Breakout is an easy to use, highly accurate, digital temperature and humidity sensor. This board has been fully calibrated and offers high precision and excellent long-term stability at low cost. The digital CMOSens® technology integrates two sensors and readout circuitry on one single chip. All you need is two lines for 2-wire communication, and you’ll have relative humidity and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
  Arduino Pro Mini v13: It's blue! It's thin! It's the Arduino Pro Mini! SparkFun's minimal design approach to Arduino. This is a 5V Arduino running the 16MHz bootloader. Arduino Pro Mini does not come with connectors populated so that you can solder in any connector or wire with any orientation you need. We recommend first time Arduino users start with the Uno R3. It's a great board that will get you up and running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
